# Fritzing sketch qt_ledvebuton (saved by Fritzing 0.8.7b)
circuit board: 8.05584cm x 6.37023cm
breadboards: 1

parts:
  Eleman1 = Arduino Uno (Rev3)
  LED1 = LED - 5mm [color="Red (633nm)" package="5 mm [THT]"]
  R1 = Resistor [tolerance=±5% resistance=220 package=THT]
  S1 = Pushbutton [package="[THT]"]

nets:
  N1: Eleman1.GND, LED1.cathode, R1.Pin_1
  N2: Eleman1.D4, R1.Pin_0, S1.Pin_1, S1.Pin_2
  N3: Eleman1.D7, LED1.anode
  N4: Eleman1.5V, S1.Pin_3, S1.Pin_4
